# Fritzing sketch schema (saved by Fritzing 0.9.4)

parts:
  WeMos_D1_Mini1 = WeMos D1 Mini
  J1 = male pin header, 8 pins [form="♂ (male)"]
  J2 = male pin header, 8 pins [form="♂ (male)"]
  J3 = male pin header, 8 pins [form="♂ (male)"]
  J4 = male pin header, 8 pins [form="♂ (male)"]
  S1 = Pushbutton [package=THT]
  JP1 = USB_MICROB_PLUG [package=micro-b-ra-smt]
  JP3 = Header 4 [package=jst-4-pth]

nets:
  N1: WeMos_D1_Mini1.3V3, S1.leg1
  5V: WeMos_D1_Mini1.5V, JP1.VCC, JP3.3, JP3.4
  N2: WeMos_D1_Mini1.A0, S1.leg0
  N3: WeMos_D1_Mini1.D0, J2.pin7
  N4: WeMos_D1_Mini1.D1, J1.pin5
  N5: WeMos_D1_Mini1.D2, J2.pin5
  N6: WeMos_D1_Mini1.D4, J1.pin8
  N7: WeMos_D1_Mini1.D5, J1.pin7
  N8: WeMos_D1_Mini1.D6, J2.pin6
  N9: WeMos_D1_Mini1.D7, J1.pin1
  N10: WeMos_D1_Mini1.D8, J1.pin6
  N11: WeMos_D1_Mini1.G, JP1.GND, JP3.2
  N12: J1.pin2, J4.pin3
  N13: J1.pin3, J3.pin1
  N14: J1.pin4, J3.pin2
  N15: J2.pin1, J3.pin3
  N16: J2.pin3, J4.pin1
  N17: J2.pin8, JP3.1
